# Fritzing sketch GIP_final (saved by Fritzing 0.8.7b)

parts:
  Mod1 = Raspberry Pi Pico
  U1 = L9110 H-bridge module [part_number="L9110 H-bridge"]
  J2 = Power Jack [package=power_jack_combo]
  BAT1 = Battery Holders [package=lipo-1100mAh]
  J3 = Basic Servo
  Part3 = Adafruit PowerBoost 1000C [part_number="Adafruit #2465"]
  S1 = SWITCH_SPDT [package=kps-1290]
  M2 = DC Motor
  D1 = SOLAR-IXYS [package=solarbit-12x1]
  D2 = Diode [package=diode-1n4001]

nets:
  N1: Mod1.pin_25, J2.PWR, D2.C
  N2: Mod1.pin_27, Part3.LBO
  N3: Mod1.pin_29, J3.pulse
  N4: Mod1.pin_31, U1.A-IB
  N5: Mod1.pin_32, U1.A-IA
  GND: Mod1.pin_33, Mod1.pin_38, Mod1.pin_42, U1.GND, J2.GND, BAT1.-, J3.gnd, Part3.GND, S1.O, D1.C
  VCC: Mod1.pin_39, U1.VCC, J3.vcc, Part3.5.0V
  N6: U1.MOTOR_A-A, M2.pin_2
  N7: U1.MOTOR_A-B, M2.pin_1
  N8: BAT1.+, Part3.VLIPO
  N9: Part3.VBUS, D1.A, D2.A
  N10: Part3.ENABLE, S1.P

notes:
  1350mAh 3.7V

custom parts:
  Raspberry Pi Pico: Raspberry Pi Pico. Based around the RP2040 microcontroller the Pico is a low cost microcontroller device bringing Raspberry Pi quality, cost, and easy of use to the microcontroller space. Jan 2021, Split part in to two versions: tht (this one) and SMD. This one will drill holes for a .1 in header in pcb to allow plugging in the module as well as providing pads to solder the module to the top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
  Adafruit PowerBoost 1000C: PowerBoost 1000C is the perfect power supply for your portable project! With a built-in load-sharing battery charger circuit, you'll be able to keep your power-hungry project running even while recharging the battery! This little DC/DC boost converter module can be powered by any 3.7V LiIon/LiPoly battery, and convert the battery output to 5.2V DC for running your 5V projects.
